# Fritzing sketch magazine_schematic (saved by Fritzing 0.9.3b)
breadboards: 1

parts:
  Part1 = Arduino Nano (Rev3.0)
  Part2 = Adafruit VL6180X Time of Flight Distance Sensor [part_number="Adafruit #3316"]
  Part3 = Bluetooth HC-05 Macho
  Part5 = I2C level shifter bidirectional

nets:
  N1: Part1.D1/TX, Part5.HV1
  N2: Part1.D0/RX, Part5.HV3
  GND: Part1.GND, Part2.GND, Part3.GND, Part5.GND
  5V: Part1.5V, Part2.VIN, Part3.VCC, Part5.HV
  N3: Part1.A5, Part2.SDA
  N4: Part1.A4, Part2.SCL
  N5: Part1.3V3, Part5.LV
  N6: Part3.TXD, Part5.LV3
  N7: Part3.RXD, Part5.LV1

custom parts:
  Adafruit VL6180X Time of Flight Distance Sensor: The VL6180X is a Time of Flight distance sensor like no other you've used! The sensor contains a very tiny invisible laser source, and a matching sensor. The VL6180X can detect the "time of flight", or how long the light has taken to bounce back to the sensor. Since it uses a very narrow light source, it is good for determining distance of only the surface directly in front of it. Unlike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
