# Fritzing sketch recievermodule (saved by Fritzing 0.9.3b)
breadboards: 1

parts:
  Part1 = Arduino Nano (Rev3.0)
  Part3 = Bluetooth HC-05 Macho
  LED1 = RGB LED - (4 legs) [package="5 mm [THT]"]
  S1 = Round Pushbutton
  R1 = Resistor [tolerance=±5% resistance=1k package=THT]
  R2 = Resistor [tolerance=±5% resistance=1k package=THT]
  R3 = Resistor [tolerance=±5% resistance=4.7k package=THT]
  R4 = Resistor [tolerance=±5% resistance=10k package=THT]

nets:
  GND: Part1.GND, Part3.GND, LED1.red_cathode, LED1.blue_cathode, R3.Pin_0, R4.Pin_1
  N1: Part1.D5, LED1.green_cathode
  N2: Part1.D8, Part3.TXD
  N3: Part1.D9, R1.Pin_1
  N4: Part1.D12/MISO, S1.leg0
  5V: Part1.5V, Part3.VCC, LED1.common_anode
  N5: Part3.RXD, R2.Pin_0, R3.Pin_1
  N6: S1.leg1, R4.Pin_0
  N7: R1.Pin_0, R2.Pin_1

notes:
  This is meant to represent a neopixel stick, and the inputs here are (left to right) GND, 5vDC, DIN, GND again.
  If you connect the VCC and KEY pins on the HC-05 it will enter AT mode if you plug it in while holding down the button on the right side of the module.
