# Fritzing sketch sensormodule (saved by Fritzing 0.9.3b)
breadboards: 1

parts:
  Part1 = Arduino Nano (Rev3.0) (ICSP)
  Part2 = Adafruit VL6180X Time of Flight Distance Sensor [part_number="Adafruit #3316"]
  Part3 = Bluetooth HC-05 Macho
  R1 = Resistor [tolerance=±5% resistance=6.8k package="0805 [SMD]"]
  R2 = Resistor [tolerance=±5% resistance=3.3k package="0805 [SMD]"]
  R3 = Resistor [tolerance=±5% resistance=10k package="0805 [SMD]"]
  R4 = Resistor [tolerance=±5% resistance=10k package="0805 [SMD]"]

nets:
  GND: Part1.GND, Part2.GND, Part3.GND, R3.Pin_1, R4.Pin_0
  N1: Part1.D8, Part3.TXD
  N2: Part1.D9, R1.Pin_0, R2.Pin_0
  5V: Part1.5V, Part2.VIN, Part3.VCC
  N3: Part1.A5, Part2.SDA
  N4: Part1.A4, Part2.SCL
  N5: Part3.RXD, R1.Pin_1, R2.Pin_1, R3.Pin_0, R4.Pin_1

custom parts:
  Adafruit VL6180X Time of Flight Distance Sensor: The VL6180X is a Time of Flight distance sensor like no other you've used! The sensor contains a very tiny invisible laser source, and a matching sensor. The VL6180X can detect the "time of flight", or how long the light has taken to bounce back to the sensor. Since it uses a very narrow light source, it is good for determining distance of only the surface directly in front of it. Unlike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
